// Logisim project 2NLP.circ as structural Verilog: 1 circuit, main circuit main
module main (
  input  S,
  input  W,
  input  D,
  input  A,
  output out_5
);

  wire and_1_out, or_1_out;

  or or_1 (or_1_out, D, W);
  and and_1 (and_1_out, or_1_out, A);
  or or_2 (out_5, and_1_out, S);
endmodule
