// Logisim project 9.circ as structural Verilog: 1 circuit, main circuit main
module main (
  input  [1:0] A,
  input  [1:0] in_2,
  output [1:0] out_3
);

  wire comparator_1_gt;

  Comparator #(.width(2)) comparator_1 (.a(in_2), .b(A), .gt(comparator_1_gt));  // open: eq, lt
  Multiplexer #(.width(2), .enable("false")) multiplexer_1 (.in0(A), .in1(in_2), .out(out_3), .sel(comparator_1_gt));

  // Notes on the sheet:
  //   B
endmodule
