// Logisim project Lab_Assignment_6.circ as structural Verilog: 5 circuits, main circuit Fig2_Mod60_Counter
module Fig1a_DFF_Register_Bit (
  input  Din,
  input  EN,
  input  RST,
  output Q
);

  wire CLK_out, multiplexer_1_out;

  Clock CLK (.out(CLK_out));
  Multiplexer multiplexer_1 (.in0(Q), .in1(Din), .out(multiplexer_1_out), .en(EN));  // open: sel
  D_Flip_Flop d_ff_1 (.clk(multiplexer_1_out), .D(CLK_out), .Q(Q), .en(RST));  // open: Qn, preset, reset

  // Notes on the sheet:
  //   Fig.1(a) D flip-flop as a 1-bit register cell: EN=1 loads Din, EN=0 holds Q (MUX feeds Q back)
endmodule

module Fig1b_Keypad_Debounce (
  input  KEY,
  input  RST,
  output Q2,
  output Y,
  output Q1
);

  wire SCLK;

  Clock u_SCLK (.out(SCLK));
  D_Flip_Flop d_ff_1 (.clk(KEY), .D(SCLK), .Q(Q1), .en(RST));  // open: Qn, preset, reset
  D_Flip_Flop d_ff_2 (.clk(Q1), .D(SCLK), .Q(Q2), .en(RST));  // open: Qn, preset, reset
  and and_1 (Y, Q1, Q2);

  // Notes on the sheet:
  //   Fig.1(b) Keypad debounce: KEY sampled by FF1 then FF2 on slow clock; Y = Q1 AND Q2
endmodule

module Fig2_Mod60_Counter (
  input  RST,
  output Q0,
  output Q1,
  output Q2,
  output Q3,
  output Q4,
  output Q5,
  output TC
);

  wire and_7_p3, and_8_p3, and_9_p3, and_10_p3, and_11_p3, and_12_p3, CLK, Qn2, T2, T3, T4, T5, TCa, TCb,
       TCc, xor_1_p3, xor_2_p3, xor_3_p3, xor_4_p3, xor_5_p3;

  Clock u_CLK (.out(CLK));
  and and_1 (T2, Q1, Q0);
  and and_2 (T3, Q2, T2);
  and and_3 (T4, Q3, T3);
  and and_4 (T5, Q4, T4);
  and and_5 (TCa, Qn2, T2);
  // XOR_Gate xor_1: pin names not known; wires that end beside it: Q1, Q0, xor_1_p3
  // XOR_Gate xor_2: pin names not known; wires that end beside it: Q2, T2, xor_2_p3
  // XOR_Gate xor_3: pin names not known; wires that end beside it: Q3, T3, xor_3_p3
  // XOR_Gate xor_4: pin names not known; wires that end beside it: Q4, T4, xor_4_p3
  // XOR_Gate xor_5: pin names not known; wires that end beside it: Q5, T5, xor_5_p3
  and and_6 (TCb, TCa, Q3);
  // AND_Gate and_7: pin names not known; wires that end beside it: Q0, TC, and_7_p3
  // AND_Gate and_8: pin names not known; wires that end beside it: xor_1_p3, TC, and_8_p3
  // AND_Gate and_9: pin names not known; wires that end beside it: xor_2_p3, TC, and_9_p3
  // AND_Gate and_10: pin names not known; wires that end beside it: xor_3_p3, TC, and_10_p3
  // AND_Gate and_11: pin names not known; wires that end beside it: xor_4_p3, TC, and_11_p3
  // AND_Gate and_12: pin names not known; wires that end beside it: xor_5_p3, TC, and_12_p3
  D_Flip_Flop d_ff_1 (.clk(and_7_p3), .D(CLK), .Q(Q0), .en(RST));  // open: Qn, preset, reset
  D_Flip_Flop d_ff_2 (.clk(and_8_p3), .D(CLK), .Q(Q1), .en(RST));  // open: Qn, preset, reset
  D_Flip_Flop d_ff_3 (.clk(and_9_p3), .D(CLK), .Q(Q2), .Qn(Qn2), .en(RST));  // open: preset, reset
  D_Flip_Flop d_ff_4 (.clk(and_10_p3), .D(CLK), .Q(Q3), .en(RST));  // open: Qn, preset, reset
  D_Flip_Flop d_ff_5 (.clk(and_11_p3), .D(CLK), .Q(Q4), .en(RST));  // open: Qn, preset, reset
  D_Flip_Flop d_ff_6 (.clk(and_12_p3), .D(CLK), .Q(Q5), .en(RST));  // open: Qn, preset, reset
  and and_13 (TCc, TCb, Q4);
  and and_14 (TC, TCc, Q5);

  // Notes on the sheet:
  //   Fig.2 Mod-60 counter (6 D flip-flops, synchronous). TC = Q5.Q4.Q3.Q2'.Q1.Q0 (count 59) clears the counter on next clock
  //   TC = 1 only at count 59 (111011). Pins Q5..Q0 give the 6-bit COUNT; Q5Q4Q3Q2Q1Q0 = binary count
endmodule

module Fig3a_SIPO_Shift_Register (
  input  SI,
  input  RST,
  output Q0,
  output Q1,
  output Q2,
  output Q3
);

  wire CLK;

  Clock u_CLK (.out(CLK));
  D_Flip_Flop d_ff_1 (.clk(SI), .D(CLK), .Q(Q0), .en(RST));  // open: Qn, preset, reset
  D_Flip_Flop d_ff_2 (.clk(Q0), .D(CLK), .Q(Q1), .en(RST));  // open: Qn, preset, reset
  D_Flip_Flop d_ff_3 (.clk(Q1), .D(CLK), .Q(Q2), .en(RST));  // open: Qn, preset, reset
  D_Flip_Flop d_ff_4 (.clk(Q2), .D(CLK), .Q(Q3), .en(RST));  // open: Qn, preset, reset

  // Notes on the sheet:
  //   Fig.3(a) 4-bit SIPO: serial data enters SI (MSB first). After 4 clocks Q3 Q2 Q1 Q0 = 1011
endmodule

module Fig3b_PISO_Shift_Register (
  input  P3,
  input  P2,
  input  P1,
  input  P0,
  input  LOAD,
  input  SI,
  input  RST,
  output Q3,
  output Q2,
  output Q1,
  output Q0,
  output SO
);

  wire CLK, multiplexer_1_out, multiplexer_2_out, multiplexer_3_out, multiplexer_4_out;

  Clock u_CLK (.out(CLK));
  Multiplexer multiplexer_1 (.in0(SI), .in1(P3), .out(multiplexer_1_out), .en(LOAD));  // open: sel
  D_Flip_Flop d_ff_1 (.clk(multiplexer_1_out), .D(CLK), .Q(Q3), .en(RST));  // open: Qn, preset, reset
  Multiplexer multiplexer_2 (.in0(Q3), .in1(P2), .out(multiplexer_2_out), .en(LOAD));  // open: sel
  D_Flip_Flop d_ff_2 (.clk(multiplexer_2_out), .D(CLK), .Q(Q2), .en(RST));  // open: Qn, preset, reset
  Multiplexer multiplexer_3 (.in0(Q2), .in1(P1), .out(multiplexer_3_out), .en(LOAD));  // open: sel
  D_Flip_Flop d_ff_3 (.clk(multiplexer_3_out), .D(CLK), .Q(Q1), .en(RST));  // open: Qn, preset, reset
  Multiplexer multiplexer_4 (.in0(Q1), .in1(P0), .out(multiplexer_4_out), .en(LOAD));  // open: sel
  D_Flip_Flop d_ff_4 (.clk(multiplexer_4_out), .D(CLK), .Q(Q0), .en(RST));  // open: Qn, preset, reset

  assign SO = Q0;

  // Notes on the sheet:
  //   Fig.3(b) 4-bit PISO: LOAD=1 loads P3..P0; LOAD=0 shifts toward Q0. SO = Q0 (LSB leaves first)
endmodule
